# Fritzing sketch annoying machine (saved by Fritzing 0.9.0b)
circuit board: 2.00779cm x 1.5502cm
breadboards: 1

parts:
  IC1 = IC, DIP package, 8 pins [chip_label=IC]
  R1 = Resistor [tolerance=±5% resistance=1k package=THT]
  R2 = Resistor [tolerance=±5% resistance=1M package=THT]
  C1 = Electrolytic Capacitor [capacitance=100µF package="100 mil [THT, electrolytic]"]
  C2 = Ceramic Capacitor [capacitance=10nF package="100 mil [THT, multilayer]"]
  J2 = female pin header, 1 pin [form="♀ (female)"]  # not connected
  J3 = female pin header, 1 pin [form="♀ (female)"]  # not connected

nets (from the schematic view):
  GND: IC1.pin1, C1.-, C2.0
  N1: IC1.pin2, IC1.pin6, R1.Pin_0, C1.+
  5V: IC1.pin4, IC1.pin8, R2.Pin_1
  N2: IC1.pin5, C2.1
  N3: IC1.pin7, R1.Pin_1, R2.Pin_0
