# Fritzing sketch Fan wiring (saved by Fritzing 0.9.1b)
circuit board: 10cm x 6cm
breadboards: 1

parts:
  Power = female pin header, 2 pins [form="♀ (female)"]
  part = female pin header, 2 pins [form="♀ (female)"]
  Dial-a-Speed = female pin header, 2 pins [form="♀ (female)"]
  Small_Swicth = Toggle Switch [package=THT]
  Small_Fan = female pin header, 2 pins [form="♀ (female)"]
  Diode = Rectifier Diode [part_number=1N4001 package="300 mil [THT]"]
  Big_Fan = female pin header, 4 pins [form="♀ (female)"]
  Big_Switch = Toggle Switch [package=THT]

nets:
  N1: Power.pin1, part.pin1, Dial-a-Speed.pin1, Small_Fan.pin1, Big_Fan.pin2
  N2: Power.pin2, Big_Switch.COM
  N3: part.pin2, Small_Swicth.L2, Big_Switch.L1
  N4: Dial-a-Speed.pin2, Small_Swicth.L1, Diode.anode
  N5: Small_Swicth.COM, Small_Fan.pin2
  N6: Diode.cathode, Big_Fan.pin1, Big_Switch.L2
