# Fritzing sketch dial-a-speed (saved by Fritzing 0.9.1b)
circuit board: 2.05458cm x 1.95297cm
breadboards: 1

parts:
  U1 = 555 Timer [package="DIP8 [THT]"]
  D1 = Rectifier Diode [part_number=1N4001 package="300 mil [THT]"]
  D2 = Rectifier Diode [part_number=1N4001 package="300 mil [THT]"]
  C1 = Ceramic Capacitor [capacitance=100nF package="100 mil [THT, multilayer]"]
  R2 = Resistor [tolerance=±5% resistance=10k package=THT]
  Q1 = Basic FET N-Channel [package="TO220 [THT]"]
  C2 = Ceramic Capacitor [capacitance=100nF package="100 mil [THT, multilayer]"]
  J1 = female pin header, 2 pins [form="♀ (female)"]
  J2 = female pin header, 3 pins [form="♀ (female)"]
  J3 = female pin header, 2 pins [form="♀ (female)"]
  D3 = Rectifier Diode [part_number=1N4001 breakdown_voltage=3.6V package="300 mil [THT]"]

nets:
  GND: U1.Ground, C1.0, Q1.source, C2.0, J3.pin2
  N1: U1.Trigger, U1.Threshold, D1.cathode, D2.anode, C2.1
  N2: U1.Output, J2.pin2
  5V: U1.Reset, U1.Vcc_Supply_Voltage, R2.Pin_1, J1.pin1, J3.pin1, D3.cathode
  N3: U1.Control_Voltage, C1.1
  N4: U1.Discharge, R2.Pin_0, Q1.gate
  N5: D1.anode, J2.pin1
  N6: D2.cathode, J2.pin3
  N7: Q1.drain, J1.pin2, D3.anode
