# Fritzing sketch fan wiring v2 (saved by Fritzing 0.9.1b)
circuit board: 10cm x 6cm
breadboards: 1

parts:
  Power = female pin header, 2 pins [form="♀ (female)"]
  J1 = female pin header, 2 pins [form="♀ (female)"]
  Dial-a-Speed = female pin header, 2 pins [form="♀ (female)"]
  Small_Fan = female pin header, 2 pins [form="♀ (female)"]
  Diode = Rectifier Diode [part_number=1N4001 package="300 mil [THT]"]
  Big_Fan = female pin header, 4 pins [form="♀ (female)"]
  Big_Switch = Toggle Switch [package=THT]
  J2 = female pin header, 5 pins [form="♀ (female)"]

nets:
  N1: Power.pin1, J1.pin1, Dial-a-Speed.pin1, Small_Fan.pin1, Big_Fan.pin2
  N2: Power.pin2, Big_Switch.COM
  N3: J1.pin2, Big_Switch.L2, J2.pin3
  N4: Dial-a-Speed.pin2, Diode.cathode, J2.pin1
  N5: Small_Fan.pin2, J2.pin5
  N6: Diode.anode, Big_Fan.pin1, Big_Switch.L1
