# Fritzing sketch drawdio v1 (saved by Fritzing 0.9.1b)
circuit board: 2.85554cm x 1.33837cm
breadboards: 1

parts:
  U1 = 555 Timer [package="DIP8 [THT]"]
  C1 = Ceramic Capacitor [capacitance=100nF package="100 mil [THT, multilayer]"]
  R2 = Resistor [tolerance=±5% resistance=10k package=THT]
  R3 = Resistor [tolerance=±5% resistance=300k package=THT]
  R4 = Resistor [tolerance=±5% resistance=10m package=THT]
  C2 = Ceramic Capacitor [capacitance=680p package="100 mil [THT, multilayer]"]
  R5 = Resistor [tolerance=±5% resistance=10m package=THT]
  J1 = female pin header, 2 pins [form="♀ (female)"]
  J3 = female pin header, 2 pins [form="♀ (female)"]
  J2 = female pin header, 2 pins [form="♀ (female)"]

nets:
  GND: U1.Ground, C1.0, R4.Pin_0, C2.0, J1.pin2, J3.pin2
  N1: U1.Trigger, U1.Threshold, R3.Pin_0, C2.1, R5.Pin_0
  N2: U1.Output, J1.pin1
  5V: U1.Reset, U1.Vcc_Supply_Voltage, R2.Pin_1, J3.pin1
  N3: U1.Control_Voltage, C1.1
  N4: U1.Discharge, R2.Pin_0, J2.pin2
  N5: R3.Pin_1, J2.pin1
  N6: R4.Pin_1, R5.Pin_1
