# Fritzing sketch Harmonica Venture (saved by Fritzing 0.9.1b)
breadboards: 1

parts:
  U1 = 555 Timer [package="DIP8 [THT]"]
  C1 = Ceramic Capacitor [capacitance=100nF package="100 mil [THT, multilayer]"]
  S1 = Pushbutton [package="[THT]"]
  S2 = Pushbutton [package="[THT]"]
  S3 = Pushbutton [package="[THT]"]
  S4 = Pushbutton [package="[THT]"]
  S5 = Pushbutton [package="[THT]"]
  C2 = Ceramic Capacitor [capacitance=100nF package="100 mil [THT, multilayer]"]
  SPKR1 = Loudspeaker
  C3 = Electrolytic Capacitor [capacitance=100µF package="100 mil [THT, electrolytic]"]
  C4 = Electrolytic Capacitor [capacitance=100µF package="100 mil [THT, electrolytic]"]
  R1 = Resistor [tolerance=±5% resistance=3.3k package=THT]
  R2 = Resistor [tolerance=±5% resistance=18k package=THT]
  R3 = Resistor [tolerance=±5% resistance=22k package=THT]
  R4 = Resistor [tolerance=±5% resistance=35k package=THT]
  R5 = Resistor [tolerance=±5% resistance=26k package=THT]
  R6 = Resistor [tolerance=±5% resistance=42 package=THT]

nets:
  GND: U1.Ground, C1.0, C2.0, SPKR1.pin2, C4.-
  N1: U1.Trigger, U1.Threshold, C2.1, R1.Pin_0
  N2: U1.Output, C3.-
  5V: U1.Reset, U1.Vcc_Supply_Voltage, S1.Pin_1, S1.Pin_2, S2.Pin_1, S2.Pin_2, S3.Pin_1, S3.Pin_2, S4.Pin_1, S4.Pin_2, S5.Pin_1, C4.+
  N3: U1.Control_Voltage, C1.1
  N4: U1.Discharge, R1.Pin_1
  N5: S1.Pin_3, S1.Pin_4, R2.Pin_1
  N6: S2.Pin_3, S2.Pin_4, R3.Pin_1
  N7: S3.Pin_3, S3.Pin_4, R4.Pin_1
  N8: S4.Pin_3, S4.Pin_4, R5.Pin_1
  N9: S5.Pin_3, S5.Pin_4, R6.Pin_1
  N10: SPKR1.pin1, C3.+
