# Fritzing sketch Cycle Switcher (saved by Fritzing 0.9.0b)
breadboards: 1

parts:
  IC1 = IC, DIP package, 16 pins [chip_label=IC]
  S1 = Pushbutton [package="[THT]"]
  R1 = Resistor [tolerance=±5% resistance=10k package=THT]
  LED2 = LED - 5mm [color="Blue (505nm)" package="5 mm [THT]"]
  LED1 = LED - 5mm [color="Red (633nm)" package="5 mm [THT]"]
  LED3 = LED - 5mm [color="Green (565nm)" package="5 mm [THT]"]

nets:
  N1: IC1.pin2, LED3.anode
  N2: IC1.pin3, LED1.anode
  N3: IC1.pin7, LED2.anode
  GND: IC1.pin8, R1.Pin_0, LED2.cathode, LED1.cathode, LED3.cathode
  N4: IC1.pin10, IC1.pin15
  N5: IC1.pin14, S1.Pin_3, S1.Pin_4, R1.Pin_1
  5V: IC1.pin16, S1.Pin_1, S1.Pin_2
