# Fritzing sketch randomventure (saved by Fritzing 0.9.1b)
circuit board: 5.31995cm x 4.117cm
breadboards: 1

parts:
  IC1 = IC, DIP package, 16 pins [chip_label=IC]
  J1 = female pin header, 3 pins [form="♀ (female)"]
  J2 = female pin header, 7 pins [form="♀ (female)"]
  C1 = Ceramic Capacitor [capacitance=100nF package="100 mil [THT, multilayer]"]
  R1 = Resistor [tolerance=±5% resistance=1k package=THT]
  R3 = Resistor [tolerance=±5% resistance=220 package=THT]
  R4 = Resistor [tolerance=±5% resistance=220 package=THT]
  R5 = Resistor [tolerance=±5% resistance=220 package=THT]
  LED1 = LED - 5mm [color="Red (633nm)" package="5 mm [THT]"]
  LED2 = LED - 5mm [color="Red (633nm)" package="5 mm [THT]"]
  LED3 = LED - 5mm [color="Red (633nm)" package="5 mm [THT]"]
  C3 = Electrolytic Capacitor [capacitance=100µF package="100 mil [THT, electrolytic]"]
  R2 = Resistor [tolerance=±5% resistance=100 package=THT]
  U1 = 555 Timer [package="DIP8 [THT]"]
  C2 = Electrolytic Capacitor [capacitance=47µF package="100 mil [THT, electrolytic]"]
  J3 = female pin header, 1 pin [form="♀ (female)"]
  J4 = female pin header, 2 pins [form="♀ (female)"]
  S2 = Toggle Switch [package=THT]
  R6 = Resistor [tolerance=±5% resistance=220 package=THT]
  J5 = female pin header, 3 pins [form="♀ (female)"]
  J6 = female pin header, 3 pins [form="♀ (female)"]
  J7 = female pin header, 1 pin [form="♀ (female)"]

nets:
  N1: IC1.pin1, J2.pin1
  N2: IC1.pin2, J2.pin2, R3.Pin_1
  N3: IC1.pin3, J2.pin3, R4.Pin_1
  N4: IC1.pin4, J2.pin4, R5.Pin_1
  N5: IC1.pin5, J2.pin5
  N6: IC1.pin6, J2.pin6
  N7: IC1.pin7, J2.pin7
  GND: IC1.pin8, C1.0, LED1.cathode, LED2.cathode, LED3.cathode, C3.-, U1.Ground, C2.-, S2.L2, R6.Pin_0
  N8: IC1.pin9, J1.pin3
  N9: IC1.pin10, J1.pin2
  N10: IC1.pin11, J1.pin1
  N11: IC1.pin13, R6.Pin_1, J5.pin3, J6.pin3
  N12: IC1.pin14, U1.Output, J7.pin1
  N13: IC1.pin15, J3.pin1
  5V: IC1.pin16, R1.Pin_1, C3.+, U1.Reset, U1.Vcc_Supply_Voltage, J4.pin2, J5.pin1, J6.pin1
  N14: C1.1, U1.Control_Voltage
  N15: R1.Pin_0, R2.Pin_1, U1.Discharge
  N16: R3.Pin_0, LED3.anode
  N17: R4.Pin_0, LED2.anode
  N18: R5.Pin_0, LED1.anode
  N19: R2.Pin_0, U1.Trigger, U1.Threshold, C2.+
  N20: J4.pin1, S2.L1, S2.COM
