# Fritzing sketch rapid click (saved by Fritzing 0.9.1b)
circuit board: 8.46667cm x 5.64444cm
breadboards: 1

parts:
  U1 = 555 Timer [package="DIP8 [THT]"]
  C1 = Ceramic Capacitor [capacitance=100nF package="100 mil [THT, multilayer]"]
  C2 = Electrolytic Capacitor [capacitance=1µF package="100 mil [THT, electrolytic]"]
  R1 = Resistor [tolerance=±5% resistance=220 package=THT]
  R2 = Resistor [tolerance=±5% resistance=220 package=THT]
  D1 = Rectifier Diode [part_number=1N4001 package="300 mil [THT]"]

nets:
  GND: U1.Ground, C1.0, C2.-
  N1: U1.Trigger, U1.Threshold, C2.+, R2.Pin_0
  N2: U1.Output, D1.anode
  5V: U1.Reset, U1.Vcc_Supply_Voltage, R1.Pin_1
  N3: U1.Control_Voltage, C1.1
  N4: U1.Discharge, R1.Pin_0, R2.Pin_1
