# Fritzing sketch attiny pov (saved by Fritzing 0.9.1b)
circuit board: 8.46667cm x 5.64444cm
breadboards: 1

parts:
  U1 = attiny85 [package=dip]
  LED1 = LED - 3mm [color="Green (560nm)" package="3 mm [THT]"]
  LED2 = LED - 3mm [color="Green (560nm)" package="3 mm [THT]"]
  LED3 = LED - 3mm [color="Green (560nm)" package="3 mm [THT]"]
  LED4 = LED - 3mm [color="Green (560nm)" package="3 mm [THT]"]
  LED5 = LED - 3mm [color="Green (560nm)" package="3 mm [THT]"]
  U2 = Voltage Regulator [package=to220-igo]
  C1 = Ceramic Capacitor [capacitance=100nF package="100 mil [THT, multilayer]"]
  C2 = Ceramic Capacitor [capacitance=100nF package="100 mil [THT, multilayer]"]

nets:
  N1: U1.Pin_2, LED5.anode
  N2: U1.Pin_3, LED1.anode
  N3: U1.Pin_4, LED1.cathode, LED2.cathode, LED3.cathode, LED4.cathode, LED5.cathode, U2.GND, C1.0, C2.1
  N4: U1.Pin_5, LED4.anode
  N5: U1.Pin_6, LED3.anode
  N6: U1.Pin_7, LED2.anode
  N7: U1.Pin_8, U2.OUT, C1.1
  N8: U2.IN, C2.0
