# Fritzing sketch halleffect (saved by Fritzing 0.9.1b)
circuit board: 10cm x 6cm
breadboards: 1

parts:
  U1 = attiny85 [package=dip]
  J1 = female pin header, 3 pins [form="♀ (female)"]
  Q1 = NPN-Transistor [package="TO92 [THT]"]
  Q2 = NPN-Transistor [package="TO92 [THT]"]
  Q3 = NPN-Transistor [package="TO92 [THT]"]
  Q4 = PNP-Transistor [package="TO92 [THT]"]
  R1 = Resistor [tolerance=±5% resistance=1k package=THT]
  R2 = Resistor [tolerance=±5% resistance=1k package=THT]
  R3 = Resistor [tolerance=±5% resistance=1k package=THT]
  R4 = Resistor [tolerance=±5% resistance=1k package=THT]
  J3 = female pin header, 2 pins [form="♀ (female)"]
  J4 = female pin header, 4 pins [form="♀ (female)"]
  J2 = female pin header, 4 pins [form="♀ (female)"]
  LED1 = LED - 3mm [color="Green (560nm)" package="3 mm [THT]"]

nets:
  N1: U1.Pin_2, R1.Pin_1
  N2: U1.Pin_3, R3.Pin_1
  GND: U1.Pin_4, J1.pin2, Q2.E, Q3.E, J3.pin2, LED1.cathode
  N3: U1.Pin_5, R4.Pin_0
  N4: U1.Pin_6, R2.Pin_0
  N5: U1.Pin_7, J1.pin3
  4.5V: U1.Pin_8, J1.pin1, Q4.E, J3.pin1, J2.pin1
  N6: Q1.E, J4.pin3
  N7: Q1.B, R2.Pin_1, LED1.anode
  N8: Q1.C, J4.pin1
  N9: Q2.B, R4.Pin_1
  N10: Q2.C, J2.pin4
  N11: Q3.B, R3.Pin_0
  N12: Q3.C, J2.pin2
  N13: Q4.B, R1.Pin_0
  N14: Q4.C, J2.pin3
