# Fritzing sketch tv-b-gone (saved by Fritzing 0.9.1b)
circuit board: 3.08639cm x 2.14584cm
breadboards: 1

parts:
  U1 = attiny85 [package=dip]
  Y1 = Resonator [frequency="8 MHz" package=THT]
  R1 = Resistor [tolerance=±5% resistance=1k package=THT]
  R2 = Resistor [tolerance=±5% resistance=1k package=THT]
  Q1 = PNP-Transistor [package="TO92 [THT]"]
  Q2 = NPN-Transistor [package="TO92 [THT]"]
  Q3 = NPN-Transistor [package="TO92 [THT]"]
  Q4 = NPN-Transistor [package="TO92 [THT]"]
  Q5 = NPN-Transistor [package="TO92 [THT]"]
  D1 = LTE-302 [package=lte-302]
  D3 = LTE-302 [package=lte-302]
  D4 = LTE-302 [package=lte-302]
  D5 = LTE-302 [package=lte-302]
  C2 = Ceramic Capacitor [capacitance=100nF package="100 mil [THT, multilayer]"]
  R3 = Resistor [tolerance=±5% resistance=10k package=THT]
  C1 = Electrolytic Capacitor [capacitance=1µF package="100 mil [THT, electrolytic]"]
  J1 = female pin header, 3 pins [form="♀ (female)"]
  J2 = female pin header, 3 pins [form="♀ (female)"]
  LED1 = LED - 3mm [color="Green (565nm)" package="3 mm [THT]"]
  VCC1 = Battery

nets:
  N1: U1.Pin_1, J1.pin1, J2.pin1
  N2: U1.Pin_2, Y1.pin_1
  N3: U1.Pin_3, Y1.0
  GND: U1.Pin_4, Y1.GND, Q2.E, Q3.E, Q4.E, Q5.E, C2.0, R3.Pin_0, C1.-, J1.pin3, J2.pin3, VCC1.-
  N4: U1.Pin_5, R2.Pin_0
  N5: U1.Pin_7, R1.Pin_0
  5V: U1.Pin_8, Q1.E, D1.A, D3.A, D4.A, D5.A, C2.1, C1.+, LED1.anode, VCC1.+
  N6: R1.Pin_1, LED1.cathode
  N7: R2.Pin_1, Q1.B
  N8: Q1.C, Q2.B, Q3.B, Q4.B, Q5.B, R3.Pin_1
  N9: Q2.C, D1.C
  N10: Q3.C, D3.C
  N11: Q4.C, D4.C
  N12: Q5.C, D5.C
