# Fritzing sketch lightingBasement (saved by Fritzing 0.9.1b)
circuit board: 3.21033cm x 2.21345cm
breadboards: 1

parts:
  RGB_SMD_LED1 = SMD RGB LED (WS2812) [package=5050]
  RGB_SMD_LED2 = SMD RGB LED (WS2812) [package=5050]
  RGB_SMD_LED4 = SMD RGB LED (WS2812) [package=5050]
  RGB_SMD_LED5 = SMD RGB LED (WS2812) [package=5050]
  RGB_SMD_LED6 = SMD RGB LED (WS2812) [package=5050]
  RGB_SMD_LED8 = SMD RGB LED (WS2812) [package=5050]
  J1 = female pin header, 3 pins [form="♀ (female)"]
  U1 = attiny85 [package=dip]
  Q1 = NPN-Transistor [package="TO92 [THT]"]
  J2 = female pin header, 2 pins [form="♀ (female)"]
  R1 = Resistor [tolerance=±5% resistance=220 package=THT]
  RGB_SMD_LED9 = SMD RGB LED (WS2812) [package=5050]
  RGB_SMD_LED3 = SMD RGB LED (WS2812) [package=5050]
  RGB_SMD_LED7 = SMD RGB LED (WS2812) [package=5050]
  Pad1 = Pad [width=14.7965039047619 height=3.91078155555555 connect=center]  # not connected
  Pad2 = Pad [width=15.239991936508 height=3.46728949206349 connect=center]

nets:
  VCC: RGB_SMD_LED1.DOut, RGB_SMD_LED1.DIn, RGB_SMD_LED1.VCC, RGB_SMD_LED2.NC, RGB_SMD_LED2.VDD, RGB_SMD_LED2.VSS, RGB_SMD_LED4.NC, RGB_SMD_LED4.VDD, RGB_SMD_LED4.VSS, RGB_SMD_LED5.DOut, RGB_SMD_LED5.DIn, RGB_SMD_LED5.VCC, RGB_SMD_LED6.NC, RGB_SMD_LED6.VDD, RGB_SMD_LED6.VSS, RGB_SMD_LED8.DOut, RGB_SMD_LED8.DIn, RGB_SMD_LED8.VCC
  VDD: RGB_SMD_LED1.NC, RGB_SMD_LED1.VDD, RGB_SMD_LED1.VSS, RGB_SMD_LED2.DOut, RGB_SMD_LED2.DIn, RGB_SMD_LED2.VCC, RGB_SMD_LED4.DOut, RGB_SMD_LED4.DIn, RGB_SMD_LED4.VCC, RGB_SMD_LED5.NC, RGB_SMD_LED5.VDD, RGB_SMD_LED5.VSS, RGB_SMD_LED6.DOut, RGB_SMD_LED6.DIn, RGB_SMD_LED6.VCC, RGB_SMD_LED8.NC, RGB_SMD_LED8.VDD, RGB_SMD_LED8.VSS, RGB_SMD_LED9.NC, RGB_SMD_LED9.VDD, RGB_SMD_LED9.VSS, RGB_SMD_LED3.NC, RGB_SMD_LED3.VDD, RGB_SMD_LED3.VSS, RGB_SMD_LED7.NC, RGB_SMD_LED7.VDD, RGB_SMD_LED7.VSS
  N1: J1.pin1, U1.Pin_8, J2.pin2, Pad2.pad
  N2: J1.pin2, U1.Pin_4, Q1.E, J2.pin1
  N3: J1.pin3, U1.Pin_5
  N4: U1.Pin_6, R1.Pin_1
  N5: Q1.B, R1.Pin_0
  VCC_2: RGB_SMD_LED9.DOut, RGB_SMD_LED9.DIn, RGB_SMD_LED9.VCC, RGB_SMD_LED3.DOut, RGB_SMD_LED3.DIn, RGB_SMD_LED3.VCC, RGB_SMD_LED7.DOut, RGB_SMD_LED7.DIn, RGB_SMD_LED7.VCC
