# Fritzing sketch Wiring (saved by Fritzing 0.9.1b)
circuit board: 4.28978cm x 3.40077cm
breadboards: 1

parts:
  J1 = female pin header, 6 pins [form="♀ (female)"]
  J2 = Generic double row female header - 8 pins [form="♀ (female)" package=THT]
  C1 = Ceramic Capacitor [capacitance=100nF package="100 mil [THT, multilayer]"]
  C2 = Electrolytic Capacitor [capacitance=1µF package="100 mil [THT, electrolytic]"]
  S1 = Pushbutton [package="[THT]"]
  S2 = Pushbutton [package="[THT]"]
  LED1 = LED - 5mm [color="Red (633nm)" package="5 mm [THT]"]
  R1 = Resistor [tolerance=±5% resistance=220 package=THT]
  R2 = Resistor [tolerance=±5% resistance=10k package=THT]
  U1 = Voltage Regulator [package=to220-igo]
  S3 = Momentary Switch [package=tactile-pth]

nets:
  DTR: J1.pin1
  RXD: J1.pin2, J2.pin5
  TXD: J1.pin3, J2.pin1
  5v: J1.pin4, U1.IN
  GND/Gnd: J1.pin5, J2.pin4, C1.1, C2.-, S1.Pin_1, S1.Pin_2, S2.Pin_1, S2.Pin_2, U1.GND, S3.3
  3v3: J1.pin6
  N1: J2.pin2, S1.Pin_3, S1.Pin_4, LED1.cathode
  N2: J2.pin3, S2.Pin_3, S2.Pin_4, R2.Pin_1, S3.1
  3.3V: J2.pin6, J2.pin8, C1.0, C2.+, R1.Pin_0, R2.Pin_0, U1.OUT
  N3: LED1.anode, R1.Pin_1

custom parts:
  Generic double row female header - 8 pins: Generic double row female header
