# Fritzing sketch fmtransmitter (saved by Fritzing 0.9.3b)
circuit board: 3.60292cm x 1.05098cm
breadboards: 1

parts:
  J1 = female pin header, 3 pins [form="♀ (female)"]
  C2 = Ceramic Capacitor [capacitance=100nF package="100 mil [THT, multilayer]"]
  Q1 = NPN-Transistor [package="TO92 [THT]"]
  C3 = Ceramic Capacitor [capacitance=100nF package="100 mil [THT, multilayer]"]
  C5 = Ceramic Capacitor [capacitance=10pF package="100 mil [THT, multilayer]"]
  V1 = DC Power [voltage=5]
  J2 = female pin header, 2 pins [form="♀ (female)"]
  R1 = Resistor [tolerance=±5% resistance=10k package="0805 [SMD]"]
  R2 = Resistor [tolerance=±5% resistance=27k package="0805 [SMD]"]
  R3 = Resistor [tolerance=±5% resistance=470 package=THT]
  L1 = Inductor [package="400 mil [THT]"]
  Part1 = Variable Capacitor [capacitance=100nF max_capacitance=10pF min_capacitance=2pF voltage=35V]
  C6 = Ceramic Capacitor [capacitance=100nF package="100 mil [THT, multilayer]"]
  C7 = Ceramic Capacitor [capacitance=100nF package="100 mil [THT, multilayer]"]

nets:
  N1: J1.pin1, J1.pin2, C6.1
  GND: J1.pin3, C2.0, C3.0, V1.V-, J2.pin2, R1.Pin_0, R3.Pin_0, C7.0
  N2: C2.1, Q1.B, R1.Pin_1, R2.Pin_0, C6.0
  N3: Q1.E, C5.0, R3.Pin_1, C7.1
  N4: Q1.C, C5.1, L1.pin_1, Part1.0
  5V: C3.1, V1.V+, J2.pin1, R2.Pin_1, L1.pin_0, Part1.2
