# Fritzing sketch Untitled Sketch 2 (saved by Fritzing 0.9.1b)
circuit board: 3.81cm x 3.14678cm
breadboards: 1

parts:
  IC1 = IC, DIP package, 8 pins [chip_label=IC]
  LED1 = LED - 5mm [color="White (8000K)" package="5 mm [THT]"]
  R1 = Resistor [tolerance=±5% resistance=330 package=THT]
  Q1 = NPN-Transistor [package="TO92 [THT]"]
  R2 = Resistor [tolerance=±5% resistance=4.7k package=THT]
  C2 = Electrolytic Capacitor [capacitance=1µF package="100 mil [THT, electrolytic]"]
  R3 = Resistor [tolerance=±5% resistance=22k package=THT]
  Q2 = NPN-Transistor [package="TO92 [THT]"]
  R4 = Resistor [tolerance=±5% resistance=10k package=THT]
  R5 = Resistor [tolerance=±5% resistance=100k package=THT]
  R7 = Resistor [tolerance=±5% resistance=4.7k package=THT]
  R8 = Resistor [tolerance=±5% resistance=330 package=THT]
  R9 = Resistor [tolerance=±5% resistance=330 package=THT]
  R10 = Resistor [tolerance=±5% resistance=330 package=THT]
  LED2 = LED - 5mm [color="White (8000K)" package="5 mm [THT]"]
  LED3 = LED - 5mm [color="White (8000K)" package="5 mm [THT]"]
  LED4 = LED - 5mm [color="White (8000K)" package="5 mm [THT]"]
  R11 = Trimmer Potentiometer [maximum_resistance=10kΩ package=THT]
  U1 = MIC [package=mic-9.7mm]
  J1 = female pin header, 2 pins [form="♀ (female)"]
  S1 = Toggle Switch [package=THT]
  C1 = Ceramic Capacitor [capacitance=100nF package="100 mil [THT, multilayer]"]

nets:
  4.5V: IC1.pin1, R1.Pin_1, R4.Pin_1, R7.Pin_1, R8.Pin_1, R9.Pin_1, R10.Pin_1, R11.leg1, R11.wiper, S1.L2, C1.1
  N1: IC1.pin2, R2.Pin_1
  N2: IC1.pin6, Q2.C, R4.Pin_0
  GND: IC1.pin8, Q1.E, R3.Pin_0, Q2.E, U1.2, J1.pin2, C1.0
  N3: LED1.cathode, Q1.C, LED2.cathode, LED3.cathode, LED4.cathode
  N4: LED1.anode, R1.Pin_0
  N5: Q1.B, R2.Pin_0
  N6: C2.-, R3.Pin_1, Q2.B, R5.Pin_0
  N7: C2.+, R7.Pin_0, U1.1
  N8: R5.Pin_1, R11.leg2
  N9: R8.Pin_0, LED2.anode
  N10: R9.Pin_0, LED3.anode
  N11: R10.Pin_0, LED4.anode
  N12: J1.pin1, S1.COM
